// Logisim project 9-bitProcessor.circ as structural Verilog: 1 circuit, main circuit main
module main (
  input  [7:0] in_1,
  input  [7:0] in_2,
  input  [1:0] in_3,
  input  [7:0] in_4,
  input  [7:0] in_5,
  input  [7:0] in_6,
  input  in_7,
  input  [7:0] in_8,
  input  in_9,
  input  in_10,
  input  [7:0] in_11,
  input  in_12,
  input  [7:0] in_13,
  input  [7:0] in_14,
  input  in_15,
  input  [7:0] in_16,
  input  in_17,
  input  in_18,
  input  [1:0] in_19,
  input  [1:0] in_20,
  input  [1:0] in_21,
  input  [3:0] in_22,
  input  [3:0] in_23,
  input  [3:0] in_24,
  input  [3:0] in_25,
  input  [3:0] in_26,
  input  [3:0] in_27,
  input  [3:0] in_28,
  input  [3:0] in_29,
  input  [3:0] in_30,
  input  [3:0] in_31,
  input  [3:0] in_32,
  input  [3:0] in_33,
  input  [3:0] in_34,
  input  [3:0] in_35,
  input  [3:0] in_36,
  input  [3:0] in_37,
  input  [1:0] in_38,
  input  [2:0] in_39,
  input  [2:0] in_40,
  input  [2:0] in_41,
  input  [8:0] in_42,
  input  [7:0] in_43,
  input  [7:0] in_44,
  input  [7:0] in_45,
  input  [7:0] in_46,
  input  [7:0] in_47,
  input  [7:0] in_48,
  input  [7:0] in_49,
  input  [7:0] in_50
);

  wire A_sel, adder_4_cout, adder_5_cout, adder_6_cout, adder_7_cout, adder_8_cout, adder_9_cout, and_1_out,
       B_sel, bitselector_2_out, bitselector_11_out, bitselector_32_out, bitselector_35_out, C_sel,
       clock_1_out, clock_2_out, clock_3_out, clock_4_out, clock_5_out, clock_6_out, clock_7_out,
       clock_8_out, clock_9_out, clock_10_out, comparator_1_gt, comparator_2_gt, decoder_1_out1,
       decoder_1_out2, decoder_1_out3, decoder_1_out4, decoder_1_out5, decoder_2_out0, decoder_2_out1,
       decoder_2_out2, decoder_2_out3, decoder_2_out4, decoder_2_out5, decoder_3_out0, decoder_3_out1,
       decoder_3_out2, decoder_3_out3, decoder_3_out4, decoder_3_out5, demultiplexer_1_out0,
       demultiplexer_1_out1, demultiplexer_1_out2, demultiplexer_1_out3, demultiplexer_1_out4,
       demultiplexer_1_out5, demultiplexer_1_out6, demultiplexer_1_out7, demultiplexer_1_out8,
       demultiplexer_1_out9, demultiplexer_1_out10, demultiplexer_1_out11, demultiplexer_5_out0,
       demultiplexer_5_out1, demultiplexer_5_out2, demultiplexer_5_out3, demultiplexer_5_out4,
       demultiplexer_5_out5, demultiplexer_5_out6, demultiplexer_5_out7, demultiplexer_8_out0,
       demultiplexer_8_out1, demultiplexer_8_out2, demultiplexer_8_out3, demultiplexer_8_out4,
       demultiplexer_8_out5, demultiplexer_8_out6, demultiplexer_8_out7, demultiplexer_8_out8,
       demultiplexer_8_out9, demultiplexer_8_out10, demultiplexer_8_out11, demultiplexer_8_out12,
       demultiplexer_8_out13, demultiplexer_8_out14, demultiplexer_8_out15, nand_1_out, nor_1_out, or_2_out,
       or_4_out, output_from_SVM_bit, PC, read_from_memory_bit, write_to_memory_bit;
  wire [1:0] a_bus_input_sel, ALU_op_sel, bitselector_3_out, bitselector_4_out, bitselector_5_out,
       bitselector_6_out, bitselector_7_out, bitselector_10_out, register_from_IR_sel_1,
       register_from_IR_sel_2;
  wire [2:0] a_register_sel, b_register_sel, bitselector_1_out, bitselector_13_out, bitselector_14_out,
       bitselector_15_out, bitselector_26_out, bitselector_27_out, bitselector_29_out, bitselector_30_out,
       bitselector_31_out, bitselector_33_out, bitselector_34_out, bitselector_36_out, c_register_sel,
       multiplexer_3_out, multiplexer_4_out, multiplexer_6_out, multiplexer_7_out, multiplexer_8_out;
  wire [3:0] adder_1_out, adder_10_out, multiplexer_1_out, multiplexer_2_out, multiplexer_11_out,
       register_1_q, register_9_q;
  wire [4:0] bitselector_8_out, bitselector_9_out, bitselector_28_out;
  wire [7:0] adder_2_out, adder_3_out, adder_4_out, adder_5_out, adder_6_out, adder_7_out, adder_8_out,
       adder_9_out, adder_11_out, adder_12_out, bitselector_12_out, bitselector_16_out,
       controlled_buffer_26_out, controlled_buffer_27_out, controlled_buffer_28_out,
       controlled_buffer_29_out, controlled_buffer_30_out, controlled_buffer_31_out,
       controlled_buffer_32_out, controlled_buffer_33_out, demultiplexer_3_out0, demultiplexer_3_out1,
       demultiplexer_3_out2, demultiplexer_4_out0, demultiplexer_4_out1, demultiplexer_6_out0,
       demultiplexer_6_out1, demultiplexer_6_out2, demultiplexer_7_out0, demultiplexer_7_out1, ledbar_3_p1,
       ledbar_4_p1, ledbar_5_p1, multiplexer_9_out, multiplexer_10_out, multiplexer_12_out,
       multiplier_1_cout, multiplier_1_out, multiplier_2_cout, multiplier_2_out, multiplier_3_cout,
       multiplier_3_out, multiplier_4_cout, multiplier_4_out, multiplier_5_cout, multiplier_5_out,
       multiplier_6_cout, multiplier_6_out, multiplier_7_cout, multiplier_7_out, multiplier_8_cout,
       multiplier_8_out, or_1_out, or_3_out, register_3_q, register_4_q, register_5_q, register_6_q,
       register_7_q, register_8_q, shifter_1_out, shifter_2_out, shifter_3_out;
  wire [8:0] bitselector_17_out, bitselector_25_out, demultiplexer_2_out0, demultiplexer_2_out1, ledbar_2_p1,
       ledbar_6_p1, ram_1_dout;
  wire [16:0] controlled_buffer_1_out;

  BitSelector #(.group(3), .width(9)) bitselector_1 (.in(ledbar_2_p1), .out(bitselector_1_out), .sel(2'b10));
  // LedBar #(.inputtype("row"), .matrixcols(3)) ledbar_1: pin names not known; wires that end beside it: bitselector_1_out
  Multiplexer #(.select(3), .width(4)) multiplexer_1 (
    .in0(4'b0010), .in1(4'b0011), .in2(4'b0100), .in3(4'b0101), .in4(4'b0110), .in5(4'b0110), .in6(4'b0111),
    .in7(4'b0111), .out(multiplexer_1_out), .sel(bitselector_1_out));
  and and_1 (and_1_out, demultiplexer_1_out3, nor_1_out);
  LED led_1 (.in(and_1_out));
  nor nor_1 (nor_1_out, ledbar_2_p1[0], ledbar_2_p1[1], ledbar_2_p1[2], ledbar_2_p1[3], ledbar_2_p1[4], ledbar_2_p1[5], ledbar_2_p1[6], ledbar_2_p1[7], ledbar_2_p1[8]);
  Multiplexer #(.select(4), .width(4)) multiplexer_2 (
    .in0(4'b0001), .in1(4'b0001), .in2(4'b0001), .in3(multiplexer_1_out), .in4(4'b1110), .in5(4'b1111),
    .in6(4'b1110), .in7(4'b1101), .in8(4'b1100), .in9(4'b1011), .in10(4'b0001), .in11(4'b1001),
    .out(multiplexer_2_out), .sel(register_1_q));  // open: in12, in13, in14, in15
  Register #(.width(4)) register_1 (
    .D(adder_1_out), .en(nand_1_out), .clk(clock_1_out), .Q(register_1_q));  // open: clr
  Adder #(.width(4)) adder_1 (.a(register_1_q), .b(multiplexer_2_out), .out(adder_1_out));  // open: cin, cout
  Clock clock_1 (.out(clock_1_out));
  nand nand_1 (nand_1_out, demultiplexer_1_out3, nor_1_out);
  BitSelector #(.width(9)) bitselector_2 (.in(ledbar_2_p1), .out(bitselector_2_out), .sel(4'b0110));
  BitSelector #(.group(2), .width(9)) bitselector_3 (.in(ledbar_2_p1), .out(bitselector_3_out), .sel(3'b000));
  BitSelector #(.group(2), .width(9)) bitselector_4 (.in(ledbar_2_p1), .out(bitselector_4_out), .sel(3'b001));
  BitSelector #(.group(2), .width(9)) bitselector_5 (.in(ledbar_2_p1), .out(bitselector_5_out), .sel(3'b010));
  // LedBar #(.inputtype("row"), .matrixcols(9)) ledbar_2: pin names not known; wires that end beside it: ledbar_2_p1
  Demultiplexer #(.select(4)) demultiplexer_1 (
    .out0(demultiplexer_1_out0), .out1(demultiplexer_1_out1), .out2(demultiplexer_1_out2),
    .out3(demultiplexer_1_out3), .out4(demultiplexer_1_out4), .out5(demultiplexer_1_out5),
    .out6(demultiplexer_1_out6), .out7(demultiplexer_1_out7), .out8(demultiplexer_1_out8),
    .out9(demultiplexer_1_out9), .out10(demultiplexer_1_out10), .out11(demultiplexer_1_out11), .in(1'b1),
    .sel(register_1_q));  // open: out12, out13, out14, out15
  BitSelector #(.group(2), .width(9)) bitselector_6 (.in(ledbar_2_p1), .out(bitselector_6_out), .sel(3'b010));
  BitSelector #(.group(2), .width(9)) bitselector_7 (.in(ledbar_2_p1), .out(bitselector_7_out), .sel(3'b001));
  BitSelector #(.group(5), .width(9)) bitselector_8 (.in(ledbar_2_p1), .out(bitselector_8_out), .sel(1'b1));
  BitSelector #(.group(5), .width(9)) bitselector_9 (.in(ledbar_2_p1), .out(bitselector_9_out), .sel(1'b0));
  BitSelector #(.group(2), .width(5)) bitselector_10 (.in(bitselector_8_out), .out(bitselector_10_out), .sel(2'b00));
  BitSelector #(.width(9)) bitselector_11 (.in(ledbar_2_p1), .out(bitselector_11_out), .sel(4'b0111));
  assign {PC, A_sel, B_sel, C_sel, read_from_memory_bit, write_to_memory_bit, output_from_SVM_bit, controlled_buffer_1_out} = demultiplexer_1_out0 ? {24{1'b0}} : 24'bz;  // Controlled_Buffer controlled_buffer_1
  assign {PC, A_sel, B_sel, C_sel, read_from_memory_bit, write_to_memory_bit, output_from_SVM_bit, controlled_buffer_1_out} = demultiplexer_1_out1 ? 24'h580140 : 24'bz;  // Controlled_Buffer controlled_buffer_2
  assign {PC, A_sel, B_sel, C_sel, read_from_memory_bit, write_to_memory_bit, output_from_SVM_bit, controlled_buffer_1_out} = demultiplexer_1_out2 ? 24'h980005 : 24'bz;  // Controlled_Buffer controlled_buffer_3
  assign {PC, A_sel, B_sel, C_sel, read_from_memory_bit, write_to_memory_bit, output_from_SVM_bit, controlled_buffer_1_out} = demultiplexer_1_out3 ? 24'h980005 : 24'bz;  // Controlled_Buffer controlled_buffer_4
  assign {PC, A_sel, B_sel, C_sel, read_from_memory_bit, write_to_memory_bit, output_from_SVM_bit, controlled_buffer_1_out} = demultiplexer_1_out4 ? 24'h608568 : 24'bz;  // Controlled_Buffer controlled_buffer_5
  assign {PC, A_sel, B_sel, C_sel, read_from_memory_bit, write_to_memory_bit, output_from_SVM_bit, controlled_buffer_1_out} = demultiplexer_1_out5 ? 24'h70fa00 : 24'bz;  // Controlled_Buffer controlled_buffer_6
  assign {PC, A_sel, B_sel, C_sel, read_from_memory_bit, write_to_memory_bit, output_from_SVM_bit, controlled_buffer_1_out} = demultiplexer_1_out6 ? 24'h72f800 : 24'bz;  // Controlled_Buffer controlled_buffer_7
  assign {PC, A_sel, B_sel, C_sel, read_from_memory_bit, write_to_memory_bit, output_from_SVM_bit, controlled_buffer_1_out} = demultiplexer_1_out7 ? 24'h582800 : 24'bz;  // Controlled_Buffer controlled_buffer_8
  assign {PC, A_sel, B_sel, C_sel, read_from_memory_bit, write_to_memory_bit, output_from_SVM_bit, controlled_buffer_1_out} = demultiplexer_1_out8 ? 24'h342800 : 24'bz;  // Controlled_Buffer controlled_buffer_9
  assign {PC, A_sel, B_sel, C_sel, read_from_memory_bit, write_to_memory_bit, output_from_SVM_bit, controlled_buffer_1_out} = demultiplexer_1_out9 ? 24'h414000 : 24'bz;  // Controlled_Buffer controlled_buffer_10
  assign {PC, A_sel, B_sel, C_sel, read_from_memory_bit, write_to_memory_bit, output_from_SVM_bit, controlled_buffer_1_out} = demultiplexer_1_out10 ? 24'h410100 : 24'bz;  // Controlled_Buffer controlled_buffer_11
  assign {PC, A_sel, B_sel, C_sel, read_from_memory_bit, write_to_memory_bit, output_from_SVM_bit, controlled_buffer_1_out} = demultiplexer_1_out11 ? 24'h70c004 : 24'bz;  // Controlled_Buffer controlled_buffer_12
  BitSelector #(.group(8), .width(5)) bitselector_12 (.in(bitselector_9_out), .out(bitselector_12_out), .sel(1'b0));
  Multiplexer #(.width(3)) multiplexer_3 (
    .in0(3'b011), .in1(3'b000), .out(multiplexer_3_out), .sel(bitselector_11_out));
  Demultiplexer #(.width(9)) demultiplexer_2 (
    .out0(demultiplexer_2_out0), .out1(demultiplexer_2_out1), .in(ledbar_6_p1), .sel(PC));
  Decoder #(.select(3)) decoder_1 (
    .out1(decoder_1_out1), .out2(decoder_1_out2), .out3(decoder_1_out3), .out4(decoder_1_out4),
    .out5(decoder_1_out5), .sel(multiplexer_4_out), .en(A_sel));  // open: out0, out6, out7
  Multiplexer #(.select(2), .width(3)) multiplexer_4 (
    .in0(a_register_sel), .in1(bitselector_14_out), .in2(bitselector_15_out), .in3(bitselector_13_out),
    .out(multiplexer_4_out), .sel(register_from_IR_sel_1));
  BitSelector #(.group(3), .width(2)) bitselector_13 (.in(bitselector_3_out), .out(bitselector_13_out), .sel(1'b0));
  BitSelector #(.group(3), .width(2)) bitselector_14 (.in(bitselector_7_out), .out(bitselector_14_out), .sel(1'b0));
  BitSelector #(.group(3), .width(2)) bitselector_15 (.in(bitselector_10_out), .out(bitselector_15_out), .sel(1'b0));
  // LedBar #(.inputtype("row")) ledbar_3: pin names not known; wires that end beside it: ledbar_3_p1
  Shifter shifter_1 (.in(bitselector_12_out), .\dist (multiplexer_3_out), .out(shifter_1_out));
  Register #(.width(9)) register_2 (
    .D(demultiplexer_2_out1), .en(PC), .clk(clock_2_out), .Q(ledbar_2_p1));  // open: clr
  Clock clock_2 (.out(clock_2_out));
  Multiplexer #(.select(2), .width(8)) multiplexer_5 (
    .in0(bitselector_16_out), .in1(multiplexer_10_out), .in2(shifter_1_out), .out(ledbar_3_p1),
    .sel(a_bus_input_sel));  // open: in3
  BitSelector #(.group(8), .width(9)) bitselector_16 (.in(demultiplexer_2_out0), .out(bitselector_16_out), .sel(1'b0));
  BitSelector #(.group(9), .width(24)) bitselector_17 (
    .in({PC, A_sel, B_sel, C_sel, read_from_memory_bit, write_to_memory_bit, output_from_SVM_bit, controlled_buffer_1_out}),
    .out(bitselector_17_out), .sel(2'b01));
  BitSelector #(.group(3), .width(24)) bitselector_18 (
    .in({PC, A_sel, B_sel, C_sel, read_from_memory_bit, write_to_memory_bit, output_from_SVM_bit, controlled_buffer_1_out}),
    .out(a_register_sel), .sel(3'b010));
  BitSelector #(.group(3), .width(24)) bitselector_19 (
    .in({PC, A_sel, B_sel, C_sel, read_from_memory_bit, write_to_memory_bit, output_from_SVM_bit, controlled_buffer_1_out}),
    .out(b_register_sel), .sel(3'b001));
  BitSelector #(.group(3), .width(24)) bitselector_20 (
    .in({PC, A_sel, B_sel, C_sel, read_from_memory_bit, write_to_memory_bit, output_from_SVM_bit, controlled_buffer_1_out}),
    .out(c_register_sel), .sel(3'b000));
  Register register_3 (.D(ledbar_3_p1), .en(1'b0), .clk(clock_3_out), .Q(register_3_q));  // open: clr
  Clock clock_3 (.out(clock_3_out));
  Register register_4 (.D(ledbar_3_p1), .en(decoder_1_out1), .clk(clock_4_out), .Q(register_4_q));  // open: clr
  Clock clock_4 (.out(clock_4_out));
  Register register_5 (.D(ledbar_3_p1), .en(decoder_1_out2), .clk(clock_5_out), .Q(register_5_q));  // open: clr
  Clock clock_5 (.out(clock_5_out));
  Register register_6 (.D(ledbar_3_p1), .en(decoder_1_out3), .clk(clock_6_out), .Q(register_6_q));  // open: clr
  Clock clock_6 (.out(clock_6_out));
  Register register_7 (.D(ledbar_3_p1), .en(decoder_1_out4), .clk(clock_7_out), .Q(register_7_q));  // open: clr
  Clock clock_7 (.out(clock_7_out));
  Register register_8 (.D(ledbar_3_p1), .en(decoder_1_out5), .clk(clock_8_out), .Q(register_8_q));  // open: clr
  Clock clock_8 (.out(clock_8_out));
  BitSelector #(.group(2), .width(9)) bitselector_21 (.in(bitselector_17_out), .out(a_bus_input_sel), .sel(3'b011));
  BitSelector #(.group(2), .width(9)) bitselector_22 (
    .in(bitselector_17_out), .out(register_from_IR_sel_1), .sel(3'b010));
  BitSelector #(.group(2), .width(9)) bitselector_23 (
    .in(bitselector_17_out), .out(register_from_IR_sel_2), .sel(3'b001));
  BitSelector #(.group(2), .width(9)) bitselector_24 (.in(bitselector_17_out), .out(ALU_op_sel), .sel(3'b000));
  // LedBar #(.inputtype("row")) ledbar_4: pin names not known; wires that end beside it: ledbar_4_p1
  // LedBar #(.inputtype("row")) ledbar_5: pin names not known; wires that end beside it: ledbar_5_p1
  assign ledbar_5_p1 = decoder_2_out0 ? register_3_q : 8'bz;  // Controlled_Buffer controlled_buffer_13
  assign ledbar_4_p1 = decoder_3_out0 ? register_3_q : 8'bz;  // Controlled_Buffer controlled_buffer_14
  assign ledbar_5_p1 = decoder_2_out1 ? register_4_q : 8'bz;  // Controlled_Buffer controlled_buffer_15
  assign ledbar_4_p1 = decoder_3_out1 ? register_4_q : 8'bz;  // Controlled_Buffer controlled_buffer_16
  assign ledbar_5_p1 = decoder_2_out2 ? register_5_q : 8'bz;  // Controlled_Buffer controlled_buffer_17
  assign ledbar_4_p1 = decoder_3_out2 ? register_5_q : 8'bz;  // Controlled_Buffer controlled_buffer_18
  assign ledbar_5_p1 = decoder_2_out3 ? register_6_q : 8'bz;  // Controlled_Buffer controlled_buffer_19
  assign ledbar_4_p1 = decoder_3_out3 ? register_6_q : 8'bz;  // Controlled_Buffer controlled_buffer_20
  assign ledbar_5_p1 = decoder_2_out4 ? register_7_q : 8'bz;  // Controlled_Buffer controlled_buffer_21
  assign ledbar_4_p1 = decoder_3_out4 ? register_7_q : 8'bz;  // Controlled_Buffer controlled_buffer_22
  assign ledbar_5_p1 = decoder_2_out5 ? register_8_q : 8'bz;  // Controlled_Buffer controlled_buffer_23
  assign ledbar_4_p1 = decoder_3_out5 ? register_8_q : 8'bz;  // Controlled_Buffer controlled_buffer_24
  BitSelector #(.group(9)) bitselector_25 (.in(ledbar_5_p1), .out(bitselector_25_out), .sel(1'b0));
  Decoder #(.select(3)) decoder_2 (
    .out0(decoder_2_out0), .out1(decoder_2_out1), .out2(decoder_2_out2), .out3(decoder_2_out3),
    .out4(decoder_2_out4), .out5(decoder_2_out5), .sel(multiplexer_6_out), .en(B_sel));  // open: out6, out7
  Multiplexer #(.select(2), .width(3)) multiplexer_6 (
    .in0(b_register_sel), .in1(bitselector_29_out), .in2(bitselector_26_out), .in3(bitselector_27_out),
    .out(multiplexer_6_out), .sel(register_from_IR_sel_1));
  Decoder #(.select(3)) decoder_3 (
    .out0(decoder_3_out0), .out1(decoder_3_out1), .out2(decoder_3_out2), .out3(decoder_3_out3),
    .out4(decoder_3_out4), .out5(decoder_3_out5), .sel(multiplexer_8_out), .en(C_sel));  // open: out6, out7
  // LedBar #(.inputtype("row"), .matrixcols(9)) ledbar_6: pin names not known; wires that end beside it: ledbar_6_p1
  BitSelector #(.group(3), .width(2)) bitselector_26 (.in(bitselector_10_out), .out(bitselector_26_out), .sel(1'b0));
  BitSelector #(.group(3), .width(2)) bitselector_27 (.in(bitselector_4_out), .out(bitselector_27_out), .sel(1'b0));
  Demultiplexer #(.select(2), .width(8)) demultiplexer_3 (
    .out0(demultiplexer_3_out0), .out1(demultiplexer_3_out1), .out2(demultiplexer_3_out2), .in(ledbar_5_p1),
    .sel(ALU_op_sel));  // open: out3
  Demultiplexer #(.width(8)) demultiplexer_4 (
    .out0(demultiplexer_4_out0), .out1(demultiplexer_4_out1), .in(ledbar_4_p1), .sel(bitselector_32_out));
  BitSelector #(.group(5)) bitselector_28 (.in(ledbar_4_p1), .out(bitselector_28_out), .sel(1'b0));
  RAM #(.addrWidth(5), .dataWidth(9), .trigger("falling")) ram_1 (
    .addr(bitselector_28_out), .we(write_to_memory_bit), .oe(read_from_memory_bit), .clk(clock_9_out),
    .din(bitselector_25_out), .dout(ram_1_dout));
  Clock clock_9 (.out(clock_9_out));
  BitSelector #(.group(3), .width(2)) bitselector_29 (.in(bitselector_6_out), .out(bitselector_29_out), .sel(1'b0));
  BitSelector #(.group(3), .width(2)) bitselector_30 (.in(bitselector_7_out), .out(bitselector_30_out), .sel(1'b0));
  Multiplexer #(.width(3)) multiplexer_7 (
    .in0(bitselector_29_out), .in1(bitselector_30_out), .out(multiplexer_7_out), .sel(bitselector_2_out));
  Multiplexer #(.select(2), .width(3)) multiplexer_8 (
    .in0(c_register_sel), .in1(multiplexer_7_out), .in3(bitselector_31_out), .out(multiplexer_8_out),
    .sel(register_from_IR_sel_2));  // open: in2
  BitSelector #(.group(3), .width(2)) bitselector_31 (.in(bitselector_5_out), .out(bitselector_31_out), .sel(1'b0));
  BitSelector #(.width(2)) bitselector_32 (.in(ALU_op_sel), .out(bitselector_32_out), .sel(1'b0));
  BitSelector #(.group(3)) bitselector_33 (.in(demultiplexer_4_out0), .out(bitselector_33_out), .sel(2'b00));
  Shifter #(.shift("lr")) shifter_2 (.in(demultiplexer_3_out0), .\dist (bitselector_33_out), .out(shifter_2_out));
  Adder adder_2 (.a(demultiplexer_3_out1), .b(demultiplexer_4_out1), .out(adder_2_out));  // open: cin, cout
  Adder adder_3 (.a(demultiplexer_3_out2), .b(8'h1), .out(adder_3_out));  // open: cin, cout
  Multiplexer #(.select(2), .width(8)) multiplexer_9 (
    .in0(shifter_2_out), .in1(adder_2_out), .in2(adder_3_out), .out(multiplexer_9_out), .sel(ALU_op_sel));  // open: in3
  Multiplexer #(.width(8)) multiplexer_10 (
    .in0(multiplexer_9_out), .in1(adder_6_out), .out(multiplexer_10_out), .sel(output_from_SVM_bit));
  assign ledbar_6_p1 = read_from_memory_bit ? ram_1_dout : 9'bz;  // Controlled_Buffer controlled_buffer_25
  assign controlled_buffer_26_out = output_from_SVM_bit ? in_43 : 8'bz;  // Controlled_Buffer controlled_buffer_26
  assign controlled_buffer_27_out = output_from_SVM_bit ? in_44 : 8'bz;  // Controlled_Buffer controlled_buffer_27
  assign controlled_buffer_28_out = output_from_SVM_bit ? in_45 : 8'bz;  // Controlled_Buffer controlled_buffer_28
  assign controlled_buffer_29_out = output_from_SVM_bit ? in_46 : 8'bz;  // Controlled_Buffer controlled_buffer_29
  assign controlled_buffer_30_out = output_from_SVM_bit ? in_47 : 8'bz;  // Controlled_Buffer controlled_buffer_30
  assign controlled_buffer_31_out = output_from_SVM_bit ? in_48 : 8'bz;  // Controlled_Buffer controlled_buffer_31
  assign controlled_buffer_32_out = output_from_SVM_bit ? in_49 : 8'bz;  // Controlled_Buffer controlled_buffer_32
  assign controlled_buffer_33_out = output_from_SVM_bit ? in_50 : 8'bz;  // Controlled_Buffer controlled_buffer_33
  Multiplier multiplier_1 (
    .a(controlled_buffer_26_out), .b(controlled_buffer_30_out), .out(multiplier_1_out),
    .cout(multiplier_1_cout));  // open: cin
  Multiplier multiplier_2 (
    .a(controlled_buffer_27_out), .b(controlled_buffer_31_out), .out(multiplier_2_out),
    .cout(multiplier_2_cout));  // open: cin
  Multiplier multiplier_3 (
    .a(controlled_buffer_28_out), .b(controlled_buffer_32_out), .out(multiplier_3_out),
    .cout(multiplier_3_cout));  // open: cin
  Multiplier multiplier_4 (
    .a(controlled_buffer_29_out), .b(controlled_buffer_33_out), .out(multiplier_4_out),
    .cout(multiplier_4_cout));  // open: cin
  Adder adder_4 (.a(multiplier_1_out), .b(multiplier_2_out), .out(adder_4_out), .cout(adder_4_cout));  // open: cin
  Adder adder_5 (.a(multiplier_3_out), .b(multiplier_4_out), .out(adder_5_out), .cout(adder_5_cout));  // open: cin
  assign or_1_out = multiplier_4_cout | multiplier_3_cout | multiplier_2_cout | multiplier_1_cout;  // OR_Gate or_1, 8 bits wide
  Adder adder_6 (.a(adder_4_out), .b(adder_5_out), .out(adder_6_out), .cout(adder_6_cout));  // open: cin
  or or_2 (or_2_out, adder_6_cout, adder_4_cout, adder_5_cout, comparator_1_gt);
  Comparator comparator_1 (.a({8{1'b0}}), .b(or_1_out), .gt(comparator_1_gt));  // open: eq, lt
  // LedBar #(.inputtype("row")) ledbar_7: pin names not known; wires that end beside it: adder_6_out
  LED led_2 (.in(or_2_out));
  Demultiplexer #(.select(3)) demultiplexer_5 (
    .out0(demultiplexer_5_out0), .out1(demultiplexer_5_out1), .out2(demultiplexer_5_out2),
    .out3(demultiplexer_5_out3), .out4(demultiplexer_5_out4), .out5(demultiplexer_5_out5),
    .out6(demultiplexer_5_out6), .out7(demultiplexer_5_out7), .in(1'b1), .sel(bitselector_34_out));
  BitSelector #(.group(3), .width(9)) bitselector_34 (.in(in_42), .out(bitselector_34_out), .sel(2'b10));
  Multiplier multiplier_5 (.a(in_1), .b(in_11), .out(multiplier_5_out), .cout(multiplier_5_cout));  // open: cin
  Multiplier multiplier_6 (.a(in_2), .b(in_13), .out(multiplier_6_out), .cout(multiplier_6_cout));  // open: cin
  Multiplier multiplier_7 (.a(in_4), .b(in_14), .out(multiplier_7_out), .cout(multiplier_7_cout));  // open: cin
  Multiplier multiplier_8 (.a(in_5), .b(in_16), .out(multiplier_8_out), .cout(multiplier_8_cout));  // open: cin
  assign or_3_out = multiplier_8_cout | multiplier_7_cout | multiplier_6_cout | multiplier_5_cout;  // OR_Gate or_3, 8 bits wide
  Adder adder_7 (.a(multiplier_5_out), .b(multiplier_6_out), .out(adder_7_out), .cout(adder_7_cout));  // open: cin
  Adder adder_8 (.a(multiplier_7_out), .b(multiplier_8_out), .out(adder_8_out), .cout(adder_8_cout));  // open: cin
  Adder adder_9 (.a(adder_7_out), .b(adder_8_out), .out(adder_9_out), .cout(adder_9_cout));  // open: cin
  or or_4 (or_4_out, adder_9_cout, adder_7_cout, adder_8_cout, comparator_2_gt);
  Comparator comparator_2 (.a({8{1'b0}}), .b(or_3_out), .gt(comparator_2_gt));  // open: eq, lt
  // LedBar #(.inputtype("row")) ledbar_8: pin names not known; wires that end beside it: demultiplexer_5_out0, demultiplexer_5_out1, demultiplexer_5_out2, demultiplexer_5_out3, adder_9_out
  LED led_3 (.in(or_4_out));
  Demultiplexer #(.select(2), .width(8)) demultiplexer_6 (
    .out0(demultiplexer_6_out0), .out1(demultiplexer_6_out1), .out2(demultiplexer_6_out2), .in(in_6),
    .sel(in_3));  // open: out3
  Demultiplexer #(.width(8)) demultiplexer_7 (
    .out0(demultiplexer_7_out0), .out1(demultiplexer_7_out1), .in(in_8), .sel(bitselector_35_out));
  BitSelector #(.width(2)) bitselector_35 (.in(in_3), .out(bitselector_35_out), .sel(1'b0));
  BitSelector #(.group(3)) bitselector_36 (.in(demultiplexer_7_out0), .out(bitselector_36_out), .sel(2'b00));
  Multiplexer #(.select(4), .width(4)) multiplexer_11 (
    .in0(in_22), .in1(in_23), .in2(in_24), .in3(in_25), .in4(in_26), .in5(in_27), .in6(in_28), .in7(in_29),
    .in8(in_30), .in9(in_31), .in10(in_32), .in11(in_33), .in12(in_34), .in13(in_35), .in14(in_36),
    .in15(in_37), .out(multiplexer_11_out), .sel(register_9_q));
  Adder #(.width(4)) adder_10 (.a(register_9_q), .b(multiplexer_11_out), .out(adder_10_out));  // open: cin, cout
  Shifter #(.shift("lr")) shifter_3 (.in(demultiplexer_6_out0), .\dist (bitselector_36_out), .out(shifter_3_out));
  Adder adder_11 (.a(demultiplexer_6_out1), .b(demultiplexer_7_out1), .out(adder_11_out));  // open: cin, cout
  Adder adder_12 (.a(demultiplexer_6_out2), .b(8'h1), .out(adder_12_out));  // open: cin, cout
  Register #(.width(4)) register_9 (.D(adder_10_out), .en(1'b1), .clk(clock_10_out), .Q(register_9_q));  // open: clr
  Clock clock_10 (.out(clock_10_out));
  Demultiplexer #(.select(4)) demultiplexer_8 (
    .out0(demultiplexer_8_out0), .out1(demultiplexer_8_out1), .out2(demultiplexer_8_out2),
    .out3(demultiplexer_8_out3), .out4(demultiplexer_8_out4), .out5(demultiplexer_8_out5),
    .out6(demultiplexer_8_out6), .out7(demultiplexer_8_out7), .out8(demultiplexer_8_out8),
    .out9(demultiplexer_8_out9), .out10(demultiplexer_8_out10), .out11(demultiplexer_8_out11),
    .out12(demultiplexer_8_out12), .out13(demultiplexer_8_out13), .out14(demultiplexer_8_out14),
    .out15(demultiplexer_8_out15), .in(1'b1), .sel(register_9_q));
  Multiplexer #(.select(2), .width(8)) multiplexer_12 (
    .in0(shifter_3_out), .in1(adder_11_out), .in2(adder_12_out), .out(multiplexer_12_out), .sel(in_3));  // open: in3
  // LedBar #(.inputtype("row")) ledbar_9: pin names not known; wires that end beside it: multiplexer_12_out

  // Notes on the sheet:
  //   in_43: initial=0x15
  //   in_44: initial=0x3
  //   in_46: initial=0x2
  //   in_47: initial=0x1
  //   in_48: initial=0x9
  //   in_49: initial=0xff
  //   in_50: initial=0x11
  //   Manual Control over Datapath
  //   from controller
  //   from controller
  //   from controller
  //   from controler
  //   Halt signal
  //   Controller
  //   add
  //   ld
  //   st
  //   sethi
  //   do nothing
  //   get PC (first time)
  //   load instruction to IR
  //   incr PC
  //   scalvs
  //   shift (step 1)
  //   shift (step 2)
  //   A
  //   A Bus
  //   Register File
  //   B Bus
  //   B
  //   C
  //   C Bus
  //   Testing instructions: 
  //   ALU (add, inc, shift)
  //   ld r0 r1 | 010000100 | 84
  //   sethi r2 5 | 101000101 | 145
  //   shift r2 3 | 111000011 | 1C3 
  //   add r1 r2 r3 | 000011011 | 1B
  //   st r3 r0 | 011110000 | F0
  //   Custom Memory Unit
  //   from controller
  //   Main program:
  //   .org 11 | 000001011 | B
  //   sethi %r1 2 | 100100010 | 122 
  //   shift %r1 3 | 110100011 | 1A3
  //   sethi %r2 6 | 101000110 | 146
  //   shift %r2 3 | 111000011 | 1C3
  //   scalvs %r1 %r2 %r3 | 001011011 | 5B
  //   sethi %r2 10 | 101001010 | 14A
  //   shift %r2 3 | 111000011 | 1C3
  //   ld %r2 %r1 | 010100100 | A4
  //   add %r1 %r3 %r3 | 000011111 | 1F
  //   sethi %r2 1 | 101000001 | 141
  //   shift %r2 3 | 111000011 | 1C3
  //   st %r3 %r2 | 011111000 | F8
  //   Result:
  //   Storage data:
  //   Vector Scalar Accelerator
  //   b = 141 | 10001101
  //   0DF | 223 or 141 + 21 + 27 + 0 + 34
  //   overflow
  //   P = (21, 3, 0, 2) | 00010101, 00000011, 00000000, 00000010
  //   W = (1, 9, 255, 17) | 00000001, 00001001, 11111111, 00010001
  //   Examples of some components of CPU:
  //   add
  //   sethi
  //   svc
  //   ld
  //   st
  //   shift
  //   ALU (custom: shift, add, inc)
endmodule
